// Digital circuit ULA.dig as structural Verilog
module ULA (
  input  [3:0] Reg,
  input  [3:0] Acc,
  input  enULA,
  output [3:0] R,
  output zero
);

  wire add_1_c_o, not_1_out;
  wire [3:0] add_1_s;

  and and_1 (zero, enULA, add_1_c_o);
  Add #(.Bits(4)) add_1 (.a(Reg), .b(Acc), .c_i(1'b0), .s(add_1_s), .c_o(add_1_c_o));
  Multiplexer #(.Bits(4)) multiplexer_1 (.sel(not_1_out), .in_0(add_1_s), .in_1(4'b0000), .out(R));
  not not_1 (not_1_out, enULA);
endmodule
