// Digital circuit Unidade de controle.dig as structural Verilog
module Unidade_de_controle (
  input  [15:0] ROM,
  output enREG,
  output enALU,
  output pcSLCT,
  output enACC,
  output accSLCT,
  output enIFNZ
);

  wire and_3_out, and_4_out, not_1_out, not_2_out, not_3_out, not_4_out;

  not not_1 (not_1_out, ROM[15]);
  not not_2 (not_2_out, ROM[14]);
  not not_3 (not_3_out, ROM[13]);
  not not_4 (not_4_out, ROM[12]);
  and and_1 (enIFNZ, ROM[12], ROM[13], ROM[14], not_1_out);
  and and_2 (accSLCT, not_4_out, not_3_out, not_2_out, ROM[15]);
  and and_3 (and_3_out, ROM[12], not_3_out, ROM[14], ROM[15]);
  or or_1 (enACC, and_4_out, and_3_out);
  and and_4 (and_4_out, not_4_out, not_3_out, not_2_out, ROM[15]);
  and and_5 (pcSLCT, ROM[12], not_3_out, not_2_out, not_1_out);
  and and_6 (enALU, not_4_out, not_3_out, not_2_out, ROM[15]);
  and and_7 (enREG, ROM[12], ROM[13], not_2_out, ROM[15]);
endmodule
