// Digital circuit intel4004.dig as structural Verilog
module intel4004 (
  input  Clock
);

  wire and_1_out, ifnz, or_1_out, ULA_zero, Unidade_de_controle_accslct, Unidade_de_controle_enacc,
       Unidade_de_controle_enalu, Unidade_de_controle_enreg, Unidade_de_controle_pcslct;
  wire [3:0] ACC_q, Banco_de_Reg_da, multiplexer_3_out, ULA_r;
  wire [11:0] bitextender_1_out, multiplexer_1_out, multiplexer_2_out, PC__plus__4_s, PC_q, ROM_d;
  wire [15:12] ROM_d_2;

  Multiplexer #(.Bits(12)) multiplexer_1 (
    .sel(or_1_out), .in_0(PC__plus__4_s), .in_1(multiplexer_2_out), .out(multiplexer_1_out));
  Multiplexer #(.Bits(12)) multiplexer_2 (.sel(ifnz), .in_0(ROM_d), .in_1(bitextender_1_out), .out(multiplexer_2_out));
  Register #(.Bits(12), .Initial(0)) PC (.D(multiplexer_1_out), .C(Clock), .en(1'b1), .Q(PC_q));
  BitExtender #(.outputBits(12)) bitextender_1 (.in(ROM_d[7:0]), .out(bitextender_1_out));
  Add #(.Bits(12)) PC__plus__4 (.a(12'h4), .b(PC_q), .c_i(1'b0), .s(PC__plus__4_s));  // open: c_o
  ROM #(.WordSize(8), .AddrBits(12), .Contents("D1 60 61 D3 62 81 60 61 72 A2 05 F0 00 00 00 00"), .AddressSize(4), .Bits(16)) ROM (
    .A(PC_q), .sel(1'b1), .D({ROM_d_2, ROM_d}));
  and and_1 (and_1_out, ifnz, ~ULA_zero);  // And
  or or_1 (or_1_out, Unidade_de_controle_pcslct, and_1_out);
  Multiplexer #(.Bits(4)) multiplexer_3 (
    .sel(Unidade_de_controle_accslct), .in_0(ROM_d[11:8]), .in_1(ULA_r), .out(multiplexer_3_out));
  Unidade_de_controle Unidade_de_controle (
    .ROM({ROM_d_2, ROM_d}), .accSLCT(Unidade_de_controle_accslct), .enACC(Unidade_de_controle_enacc),
    .enALU(Unidade_de_controle_enalu), .enREG(Unidade_de_controle_enreg), .enIFNZ(ifnz),
    .pcSLCT(Unidade_de_controle_pcslct));
  // Probe on multiplexer_3_out
  Register #(.Bits(4), .Initial(0)) ACC (.D(multiplexer_3_out), .C(Clock), .en(Unidade_de_controle_enacc), .Q(ACC_q));
  // Probe on ACC_q
  ULA ULA (.Reg(Banco_de_Reg_da), .Acc(ACC_q), .R(ULA_r), .zero(ULA_zero), .enULA(Unidade_de_controle_enalu));
  RegisterFile #(.AddrBits(4), .Bits(4)) Banco_de_Reg (
    .Din(ACC_q), .we(Unidade_de_controle_enreg), .Rw(ROM_d[11:8]), .C(Clock), .Ra(ROM_d[11:8]), .Rb(4'b0001),
    .Da(Banco_de_Reg_da));  // open: Db
  // Probe on Banco_de_Reg_da

  // Notes on the sheet:
  //   Clock: Hz: 1Hz
  //   contents of ROM (hex, n*v repeats v):
  //   4*0,d000,0,0,0,b000,0,0,0,d100,0,0,0,b100,400,0,0,d000,0,0,0,b300
  //   ,200,0,0,dc00,0,0,0,8300,0,0,0,b500,0,0,0,d000,0,0,0,8500,0,0,0
  //   ,d100,0,0,0,8500,0,0,0,7540,0,0,0,108c,0,0,0,d000,0,0,0,8000,0,0,0
  //   ,8100,0,0,0,b200,0,0,0,d000,0,0,0,8100,0,0,0,b000,0,0,0,d000,0,0,0
  //   ,8200,0,0,0,b100,0,0,0,d100,0,0,0,8300,0,0,0,b300,0,0,0,731d,0,0,0
  //   ,d000,0,0,0,d100,0,0,0,8300,0,0,0,731c,0,0,0,101c,0,0,0,100
endmodule
